# Fritzing sketch sketch (saved by Fritzing 0.9.3b)
breadboards: 1

parts:
  Part1 = Arduino Uno (Rev3)
  LCD1 = LCD screen
  J1 = Piezo Speaker
  Part2 = Real Time Clock Module - DS1307 RTC Breakout Board
  S1 = Pushbutton [package="[THT]"]
  S2 = Pushbutton [package="[THT]"]
  S3 = Pushbutton [package="[THT]"]
  R1 = Photocell (LDR) [package=THT]
  U2 = POT [package=pot_alpha_rv16af-20]

nets:
  N1: Part1.A0, R1.pin_0
  N2: Part1.A4/SDA, Part2.SDA
  N3: Part1.A5/SCL, Part2.SCL
  N4: Part1.D8, S1.Pin_1, S1.Pin_2
  N5: Part1.D9_PWM, S2.Pin_1, S2.Pin_2
  N6: Part1.D10_PWM/SS, S3.Pin_1, S3.Pin_2
  N7: Part1.D12/MISO, J1.pin1
  N8: Part1.D2, LCD1.DB7
  N9: Part1.D3_PWM, LCD1.DB6
  N10: Part1.D4, LCD1.DB5
  N11: Part1.D5_PWM, LCD1.DB4
  N12: Part1.D6_PWM, LCD1.E
  N13: Part1.D7, LCD1.RS
  5V: Part1.5V, LCD1.VDD, LCD1.LED+, Part2.5V, R1.pin_1, U2.E
  GND: Part1.GND, LCD1.VSS, LCD1.R/W, LCD1.LED-, J1.pin2, Part2.GND, S1.Pin_3, S1.Pin_4, S2.Pin_3, S2.Pin_4, S3.Pin_3, S3.Pin_4, U2.A
  N14: LCD1.V0, U2.S
